# Fritzing sketch General Wiring (saved by Fritzing 0.9.3b)
breadboards: 1

parts:
  Composant1 = Arduino Uno (Rev3)
  DRV_1 = DRV 8825 Stepper Motor Carrier, High Current [part_number="DRV 8825"]
  IC1 = Voltage Regulator [package=78xxl]
  BAT1 = Battery Holders [package=lipo-1100mAh]
  M1 = Stepper Motor - Bipolar

nets:
  N1: Composant1.D11_PWM/MOSI, DRV_1.STEP
  N2: Composant1.D12/MISO, DRV_1.DIRECTION
  GND: Composant1.GND, DRV_1.GROUND_ST/_MT, DRV_1.GROUND_LOG, IC1.GND, BAT1.-
  N3: Composant1.D2, DRV_1.SLEEP
  N4: Composant1.5V, IC1.OUT
  N5: DRV_1.VOLTAGE_ST/_MT, IC1.IN, BAT1.+
  N6: DRV_1.OUT_2B, M1.A
  N7: DRV_1.OUT_2A, M1.C
  N8: DRV_1.OUT_1A, M1.B
  N9: DRV_1.OUT_1B, M1.D
